// Logisim project LC-2200-16.circ as structural Verilog: 4 circuits, main circuit main
module main (
  input  in_1,
  input  in_2,
  input  in_3,
  input  in_4,
  input  in_5,
  input  in_6,
  input  in_7,
  input  in_8,
  input  in_9,
  input  in_10,
  input  in_11,
  input  in_12,
  input  in_13,
  input  in_14,
  input  in_15,
  input  in_16,
  input  in_17,
  input  in_18,
  output [15:0] out_19,
  output [15:0] out_20,
  output out_21
);

  wire Clk, nor_1_out;
  wire [3:0] RegNum;
  wire [15:0] A_q, B_q, bit_extender_1_out, IRVal, MAR_q, n16_bit_alu_1_out_4, PC_q, ram_2_data;

  Clock clock_1 (.out(Clk));
  Register #(.width(16)) PC (.D(out_19), .en(in_2), .Q(PC_q), .clk(Clk), .clr(in_18));
  assign out_19 = in_1 ? PC_q : 16'bz;  // Controlled_Buffer controlled_buffer_1
  Register #(.width(16)) A (.D(out_19), .en(in_5), .Q(A_q), .clk(Clk), .clr(in_18));
  _16_bit_ALU u_16_bit_alu_1 (.in_1(B_q), .in_2(A_q), .in_3({in_6, in_3}), .out_4(n16_bit_alu_1_out_4));
  assign out_19 = in_4 ? n16_bit_alu_1_out_4 : 16'bz;  // Controlled_Buffer controlled_buffer_2
  Register #(.width(16)) B (.D(out_19), .en(in_8), .Q(B_q), .clk(Clk), .clr(in_18));
  RAM #(.addrWidth(4), .dataWidth(16), .bus("separate")) ram_1 (
    .addr(RegNum), .din(out_19), .data(out_20), .str(in_17), .clk(Clk), .ld(1'b1), .clr(in_18));  // open: sel
  assign out_19 = in_7 ? out_20 : 16'bz;  // Controlled_Buffer controlled_buffer_3
  Register #(.width(16)) MAR (.D(out_19), .en(in_11), .Q(MAR_q), .clk(Clk), .clr(in_18));
  Multiplexer #(.select(2), .width(4), .disabled(0), .enable("false")) multiplexer_1 (
    .in0(IRVal[12:9]), .in1(IRVal[8:5]), .in2(IRVal[3:0]), .out(RegNum), .sel({in_12, in_9}));  // open: in3
  RAM #(.addrWidth(16), .dataWidth(16), .bus("separate")) ram_2 (
    .addr(MAR_q), .din(out_19), .data(ram_2_data), .str(in_15), .clk(Clk), .ld(1'b1), .clr(in_18));  // open: sel
  assign out_19 = in_10 ? ram_2_data : 16'bz;  // Controlled_Buffer controlled_buffer_4
  Register #(.width(16)) IR (.D(out_19), .en(in_14), .Q(IRVal), .clk(Clk), .clr(in_18));
  assign bit_extender_1_out = {{11{IRVal[4]}}, IRVal[4:0]};  // Bit_Extender bit_extender_1
  Register #(.width(1)) Z (.D(nor_1_out), .en(in_16), .Q(out_21), .clk(Clk), .clr(in_18));
  nor nor_1 (nor_1_out, out_19[15], out_19[14], out_19[13], out_19[12], out_19[11], out_19[10], out_19[9], out_19[8], out_19[6], out_19[5], out_19[4], out_19[3], out_19[2], out_19[1], out_19[0], out_19[7]);
  assign out_19 = in_13 ? bit_extender_1_out : 16'bz;  // Controlled_Buffer controlled_buffer_5

  // Other names for the same wires on the sheet: ALULo = in_3; ALUSel[1:0] = {in_6, in_3}; ALUHi = in_6;
  //   BUS[15:0] = out_19; Clr = in_18; DrALU = in_4; DrMEM = in_10; DrOFF = in_13; DrPC = in_1; DrREG = in_7;
  //   LdA = in_5; LdB = in_8; LdIR = in_14; LdMAR = in_11; LdPC = in_2; LdZ = in_16; Offset[4:0] = IRVal[4:0];
  //   RZ[3:0] = IRVal[3:0]; OpCode[2:0] = IRVal[15:13]; RegSel[1:0] = {in_12, in_9}; RegSelLo = in_9;
  //   RegSelHi = in_12; RegVal[15:0] = out_20; RX[3:0] = IRVal[12:9]; RY[3:0] = IRVal[8:5]; WrMEM = in_15;
  //   WrREG = in_17; Z = out_21
endmodule

module _1_bit_adder (
  input  in_1,
  input  in_2,
  input  in_3,
  output out_4,
  output out_5
);

  wire and_1_out, and_2_out, xor_1_out;

  and and_1 (and_1_out, in_1, in_2);
  xor xor_1 (xor_1_out, in_1, in_2);
  and and_2 (and_2_out, xor_1_out, in_3);
  xor xor_2 (out_4, xor_1_out, in_3);
  or or_1 (out_5, and_2_out, and_1_out);

  // Other names for the same wires on the sheet: A = in_1; B = in_2; C_IN = in_3; C_OUT = out_5; S = out_4
endmodule

module _16_bit_adder (
  input  [15:0] in_1,
  input  [15:0] in_2,
  input  in_3,
  output [15:0] out_4,
  output out_5
);

  wire n1_bit_adder_2_out_5, n1_bit_adder_3_out_5, n1_bit_adder_4_out_5, n1_bit_adder_5_out_5,
       n1_bit_adder_6_out_5, n1_bit_adder_7_out_5, n1_bit_adder_8_out_5, n1_bit_adder_9_out_5,
       n1_bit_adder_10_out_5, n1_bit_adder_11_out_5, n1_bit_adder_12_out_5, n1_bit_adder_13_out_5,
       n1_bit_adder_14_out_5, n1_bit_adder_15_out_5, n1_bit_adder_16_out_5;

  _1_bit_adder u_1_bit_adder_1 (
    .in_1(n1_bit_adder_2_out_5), .in_2(in_2[15]), .in_3(in_1[15]), .out_4(out_4[15]), .out_5(out_5));
  _1_bit_adder u_1_bit_adder_2 (
    .in_1(n1_bit_adder_4_out_5), .in_2(in_2[14]), .in_3(in_1[14]), .out_4(out_4[14]),
    .out_5(n1_bit_adder_2_out_5));
  _1_bit_adder u_1_bit_adder_3 (
    .in_1(n1_bit_adder_5_out_5), .in_2(in_2[12]), .in_3(in_1[12]), .out_4(out_4[12]),
    .out_5(n1_bit_adder_3_out_5));
  _1_bit_adder u_1_bit_adder_4 (
    .in_1(n1_bit_adder_3_out_5), .in_2(in_2[13]), .in_3(in_1[13]), .out_4(out_4[13]),
    .out_5(n1_bit_adder_4_out_5));
  _1_bit_adder u_1_bit_adder_5 (
    .in_1(n1_bit_adder_6_out_5), .in_2(in_2[11]), .in_3(in_1[11]), .out_4(out_4[11]),
    .out_5(n1_bit_adder_5_out_5));
  _1_bit_adder u_1_bit_adder_6 (
    .in_1(n1_bit_adder_7_out_5), .in_2(in_2[10]), .in_3(in_1[10]), .out_4(out_4[10]),
    .out_5(n1_bit_adder_6_out_5));
  _1_bit_adder u_1_bit_adder_7 (
    .in_1(n1_bit_adder_8_out_5), .in_2(in_2[9]), .in_3(in_1[9]), .out_4(out_4[9]),
    .out_5(n1_bit_adder_7_out_5));
  _1_bit_adder u_1_bit_adder_8 (
    .in_1(n1_bit_adder_9_out_5), .in_2(in_2[8]), .in_3(in_1[8]), .out_4(out_4[8]),
    .out_5(n1_bit_adder_8_out_5));
  _1_bit_adder u_1_bit_adder_9 (
    .in_1(n1_bit_adder_10_out_5), .in_2(in_2[7]), .in_3(in_1[7]), .out_4(out_4[7]),
    .out_5(n1_bit_adder_9_out_5));
  _1_bit_adder u_1_bit_adder_10 (
    .in_1(n1_bit_adder_12_out_5), .in_2(in_2[6]), .in_3(in_1[6]), .out_4(out_4[6]),
    .out_5(n1_bit_adder_10_out_5));
  _1_bit_adder u_1_bit_adder_11 (
    .in_1(n1_bit_adder_13_out_5), .in_2(in_2[4]), .in_3(in_1[4]), .out_4(out_4[4]),
    .out_5(n1_bit_adder_11_out_5));
  _1_bit_adder u_1_bit_adder_12 (
    .in_1(n1_bit_adder_11_out_5), .in_2(in_2[5]), .in_3(in_1[5]), .out_4(out_4[5]),
    .out_5(n1_bit_adder_12_out_5));
  _1_bit_adder u_1_bit_adder_13 (
    .in_1(n1_bit_adder_14_out_5), .in_2(in_2[3]), .in_3(in_1[3]), .out_4(out_4[3]),
    .out_5(n1_bit_adder_13_out_5));
  _1_bit_adder u_1_bit_adder_14 (
    .in_1(n1_bit_adder_16_out_5), .in_2(in_2[2]), .in_3(in_1[2]), .out_4(out_4[2]),
    .out_5(n1_bit_adder_14_out_5));
  _1_bit_adder u_1_bit_adder_15 (
    .in_1(in_3), .in_2(in_2[0]), .in_3(in_1[0]), .out_4(out_4[0]), .out_5(n1_bit_adder_15_out_5));
  _1_bit_adder u_1_bit_adder_16 (
    .in_1(n1_bit_adder_15_out_5), .in_2(in_2[1]), .in_3(in_1[1]), .out_4(out_4[1]),
    .out_5(n1_bit_adder_16_out_5));

  // Other names for the same wires on the sheet: A[15:0] = in_1; B[15:0] = in_2; C_IN = in_3; C_OUT = out_5;
  //   S[15:0] = out_4
endmodule

module _16_bit_ALU (
  input  [15:0] in_1,
  input  [15:0] in_2,
  input  [1:0] in_3,
  output [15:0] out_4
);

  wire [15:0] and_1_out, n16_bit_adder_1_out_4, n16_bit_adder_2_out_4, nand_1_out, not_1_out;

  _16_bit_adder u_16_bit_adder_1 (.in_1(in_1), .in_2(in_2), .in_3(1'b0), .out_4(n16_bit_adder_1_out_4));  // open: out_5
  assign and_1_out = in_1 & not_1_out;  // AND_Gate and_1, 16 bits wide
  assign not_1_out = ~in_2;  // NOT_Gate not_1, 16 bits wide
  _16_bit_adder u_16_bit_adder_2 (
    .in_1(in_1), .in_2(16'h1), .in_3(1'b0), .out_4(n16_bit_adder_2_out_4));  // open: out_5
  assign nand_1_out = ~(in_1 & in_2);  // NAND_Gate nand_1, 16 bits wide
  Multiplexer #(.select(2), .width(16), .disabled(0), .enable("false")) multiplexer_1 (
    .in0(n16_bit_adder_1_out_4), .in1(and_1_out), .in2(n16_bit_adder_2_out_4), .in3(nand_1_out), .out(out_4),
    .sel(in_3));

  // Other names for the same wires on the sheet: A[15:0] = in_1; B[15:0] = in_2; Out[15:0] = out_4; Sel[1:0] = in_3

  // Notes on the sheet:
  //   Add
  //   Sub
  //   Incr
  //   Nand
endmodule
